// Logisim project Plugboard.circ as structural Verilog: 1 circuit, main circuit main
module main (
  input  [5:0] in_1,
  output [5:0] out_2
);

  ROM #(.addrWidth(6), .dataWidth(6)) rom_1 (.addr(in_1), .data(out_2));

  // Notes on the sheet:
  //   contents of rom_1 (hex, n*v repeats v):
  //   15 12 6 b 4 14 2 19 d 9 c 3 a 8 16 f 10 17 1 13 5 0 e 11 18 7 1a 1b 1c 1d 1e 1f
endmodule
