// Logisim project complete_bw.circ as structural Verilog: 1 circuit, main circuit main
module main (
  input  [5:0] in_1,
  input  [5:0] in_2,
  input  [1:0] SEL,
  output [5:0] out_4
);

  wire comparator_1_eq, comparator_1_gt, comparator_2_lt, or_1_out;
  wire [4:0] multiplexer_2_out, rom_1_data, rom_2_data, rom_3_data;
  wire [5:0] adder_1_out, adder_2_out, bit_extender_1_out, bit_extender_2_out, bit_extender_3_out,
       bit_extender_4_out, multiplexer_1_out, multiplexer_3_out, subtractor_1_out;

  // Probe on in_1
  // Probe on in_2
  // Probe on out_4
  Bit_Extender #(.in_width(6), .out_width(6), .\type ("zero")) bit_extender_1 (.in(in_1), .out(bit_extender_1_out));
  Bit_Extender #(.in_width(6), .out_width(6), .\type ("zero")) bit_extender_2 (.in(in_2), .out(bit_extender_2_out));
  Adder #(.width(6)) adder_1 (.a(bit_extender_1_out), .b(bit_extender_2_out), .out(adder_1_out));  // open: cin, cout
  Comparator #(.mode("unsigned"), .width(6)) comparator_1 (
    .a(adder_1_out), .b(6'b011010), .gt(comparator_1_gt), .eq(comparator_1_eq));  // open: lt
  Subtractor #(.width(6)) subtractor_1 (.a(adder_1_out), .b(6'b011010), .out(subtractor_1_out));  // open: bin, bout
  or or_1 (or_1_out, comparator_1_gt, comparator_1_eq);
  Multiplexer #(.width(6)) multiplexer_1 (
    .in0(adder_1_out), .in1(subtractor_1_out), .out(multiplexer_1_out), .sel(or_1_out));
  ROM #(.addrWidth(5), .dataWidth(5)) rom_1 (.addr(multiplexer_1_out[4:0]), .data(rom_1_data));
  ROM #(.addrWidth(5), .dataWidth(5)) rom_2 (.addr(multiplexer_1_out[4:0]), .data(rom_2_data));
  ROM #(.addrWidth(5), .dataWidth(5)) rom_3 (.addr(multiplexer_1_out[4:0]), .data(rom_3_data));
  Multiplexer #(.select(2), .width(5)) multiplexer_2 (
    .in0(rom_1_data), .in1(rom_2_data), .in2(rom_3_data), .out(multiplexer_2_out), .sel(SEL));  // open: in3
  Comparator #(.mode("unsigned"), .width(5)) comparator_2 (
    .a(multiplexer_2_out), .b(in_2[4:0]), .lt(comparator_2_lt));  // open: gt, eq
  assign bit_extender_3_out = {{1{1'b0}}, multiplexer_2_out};  // Bit_Extender bit_extender_3
  Bit_Extender #(.in_width(6), .out_width(6), .\type ("zero")) bit_extender_4 (.in(in_2), .out(bit_extender_4_out));
  Adder #(.width(6)) adder_2 (.a(bit_extender_3_out), .b(6'b011010), .out(adder_2_out));  // open: cin, cout
  Multiplexer #(.width(6)) multiplexer_3 (
    .in0(bit_extender_3_out), .in1(adder_2_out), .out(multiplexer_3_out), .sel(comparator_2_lt));
  Subtractor #(.width(6)) subtractor_2 (.a(multiplexer_3_out), .b(bit_extender_4_out), .out(out_4));  // open: bin, bout
  // Pins of 5 and 6 bits meet at in_2

  // Notes on the sheet:
  //   contents of rom_1 (hex, n*v repeats v):
  //   14 16 18 6 0 3 5 f 15 19 1 4 2 a c 13 7 17 12 b 11 8 d 10 e 9 1a 1b 1c 1d 1e 1f
  //   contents of rom_2 (hex, n*v repeats v):
  //   0 9 f 2 19 16 11 b 5 1 3 a e 13 18 14 10 6 4 d 7 17 6 8 15 12 1a 1b 1c 1d 1e 1f
  //   contents of rom_3 (hex, n*v repeats v):
  //   13 0 6 1 f 2 12 3 10 4 14 5 15 d 19 7 18 8 17 9 10 b 11 a e c 1a 1b 1c 1d 1e 1f
endmodule
