// Logisim project digital_enigma.circ as structural Verilog: 10 circuits, main circuit main
module main (
  input  CLK,
  input  RST,
  input  KEYPRESS,
  input  in_4,
  output [5:0] out_5,
  output [5:0] CHAR_OUT,
  output out_7
);

  wire keyboard_1_avail, not_1_out, not_2_out, not_3_out;
  wire [5:0] cipher_path_1_char_out, stepping_1_pos1, stepping_1_pos2, stepping_1_pos3;
  wire [6:0] keyboard_1_data, rom_1_data;
  wire [7:0] bit_extender_1_out;
  wire [7:6] subtractor_1_out;

  Keyboard #(.buflen(10)) keyboard_1 (
    .re(KEYPRESS), .clr(not_1_out), .avail(keyboard_1_avail), .data(keyboard_1_data));  // open: clk
  not not_1 (not_1_out, RST);
  assign bit_extender_1_out = {{1{1'b0}}, keyboard_1_data};  // Bit_Extender bit_extender_1
  TTY tty_1 (.data(rom_1_data), .clk(keyboard_1_avail), .we(in_4), .clr(not_3_out));
  Subtractor subtractor_1 (.a(bit_extender_1_out), .b(8'h61), .out({subtractor_1_out, out_5}));  // open: bin, bout
  Register #(.width(1)) valid_reg (.D(KEYPRESS), .clk(CLK), .Q(out_7));  // open: en, clr
  Register #(.width(6)) out_reg (.D(cipher_path_1_char_out), .en(KEYPRESS), .clk(CLK), .Q(CHAR_OUT), .clr(not_2_out));
  not not_2 (not_2_out, RST);
  Stepping stepping_1 (
    .CLK(CLK), .RST(RST), .KEYPRESS(KEYPRESS), .POS1(stepping_1_pos1), .POS2(stepping_1_pos2),
    .POS3(stepping_1_pos3));
  ROM #(.addrWidth(6), .dataWidth(7)) rom_1 (.addr(CHAR_OUT), .data(rom_1_data));
  Cipher_path cipher_path_1 (
    .CHAR_IN(out_5), .pos1(stepping_1_pos1), .pos2(stepping_1_pos2), .pos3(stepping_1_pos3),
    .CHAR_OUT(cipher_path_1_char_out));
  not not_3 (not_3_out, RST);

  // Notes on the sheet:
  //   in_4: initial=0x1
  //   contents of rom_1 (hex, n*v repeats v):
  //   61 62 63 64 65 66 67 68 69 6a 6b 6c 6d 6e 6f 70 71 72 73 74 75 76 77 78 79 7a
endmodule

module display_decoder (
  input  [5:0] CHAR_IN
);

  wire sA, sB, sC, sD, sE, sF, sG;

  ROM #(.addrWidth(6), .dataWidth(7)) rom_1 (.addr(CHAR_IN), .data({sA, sB, sC, sD, sE, sF, sG}));
  _7_Segment_Display u_7_segment_display_1 (.g(sG), .f(sF), .a(sA), .b(sB), .e(sE), .d(sD), .c(sC));  // open: dp

  // Notes on the sheet:
  //   contents of rom_1 (hex, n*v repeats v):
  //   77 1f 4e 3d 4f 47 5f 37 6 3c 37 e 76 15 3f 67 73 5 5b f 3e 1c 14 37 33 6d
endmodule

module Cipher_path (
  input  [5:0] CHAR_IN,
  input  [5:0] pos1,
  input  [5:0] pos2,
  input  [5:0] pos3,
  output [5:0] CHAR_OUT
);

  wire [5:0] bx0_out_4, bx1_out_4, bx2_out_4, fx0_out_4, fx1_out_4, fx2_out_4, plugboard_1_char_out,
       reflector_1_char_out;

  plugboard plugboard_1 (.CHAR_IN(CHAR_IN), .CHAR_OUT(plugboard_1_char_out));
  rotor_fw fx2 (.CHAR_IN(plugboard_1_char_out), .POS(pos1), .SEL(2'b10), .out_4(fx2_out_4));
  rotor_fw fx1 (.CHAR_IN(fx2_out_4), .POS(pos2), .SEL(2'b01), .out_4(fx1_out_4));
  rotor_fw fx0 (.CHAR_IN(fx1_out_4), .POS(pos3), .SEL(2'b00), .out_4(fx0_out_4));
  reflector reflector_1 (.CHAR_IN(fx0_out_4), .CHAR_OUT(reflector_1_char_out));
  rotor_bw bx0 (.CHAR_IN(reflector_1_char_out), .POS(pos3), .SEL(2'b00), .out_4(bx0_out_4));
  rotor_bw bx1 (.CHAR_IN(bx0_out_4), .POS(pos2), .SEL(2'b01), .out_4(bx1_out_4));
  rotor_bw bx2 (.CHAR_IN(bx1_out_4), .POS(pos1), .SEL(2'b10), .out_4(bx2_out_4));
  plugboard plugboard_2 (.CHAR_IN(bx2_out_4), .CHAR_OUT(CHAR_OUT));

  // Notes on the sheet:
  //   Cipher_path
endmodule

module Stepping (
  input  CLK,
  input  RST,
  input  KEYPRESS,
  output [5:0] POS1,
  output [5:0] POS2,
  output [5:0] POS3
);

  wire and_1_out, and_2_out, comparator_1_eq, comparator_2_eq, not_1_out, or_1_out;

  not not_1 (not_1_out, RST);
  Counter #(.max('h19), .width(6)) Rotor_III (
    .clr(not_1_out), .up(KEYPRESS), .clk(CLK), .Q(POS1));  // open: load, count, D, carry
  Counter #(.max('h3f), .width(6)) Rotor_II (
    .clr(not_1_out), .count(and_1_out), .clk(CLK), .Q(POS2));  // open: load, up, D, carry
  Counter #(.max('h19), .width(6)) Rotor_I (
    .clr(not_1_out), .count(and_2_out), .clk(CLK), .Q(POS3));  // open: load, up, D, carry
  Comparator #(.mode("unsigned"), .width(6)) comparator_1 (
    .a(POS1), .b(6'b010101), .eq(comparator_1_eq));  // open: gt, lt
  Comparator #(.mode("unsigned"), .width(6)) comparator_2 (
    .a(POS2), .b(6'b001100), .eq(comparator_2_eq));  // open: gt, lt
  or or_1 (or_1_out, comparator_1_eq, comparator_2_eq);
  and and_1 (and_1_out, or_1_out, KEYPRESS);
  and and_2 (and_2_out, comparator_2_eq, KEYPRESS);
endmodule

module rotor_bw (
  input  [5:0] CHAR_IN,
  input  [5:0] POS,
  input  [1:0] SEL,
  output [5:0] out_4
);

  wire [5:0] mod26_add_1_s, multiplexer_1_out, rom_1_data, rom_2_data, rom_3_data;

  mod26_add mod26_add_1 (.A(CHAR_IN), .B(POS), .S(mod26_add_1_s));  // open: out_3, out_5
  ROM #(.addrWidth(6), .dataWidth(6)) rom_1 (.addr(mod26_add_1_s), .data(rom_1_data));
  ROM #(.addrWidth(6), .dataWidth(6)) rom_2 (.addr(mod26_add_1_s), .data(rom_2_data));
  ROM #(.addrWidth(6), .dataWidth(6)) rom_3 (.addr(mod26_add_1_s), .data(rom_3_data));
  Multiplexer #(.select(2), .width(6)) multiplexer_1 (
    .in0(rom_1_data), .in1(rom_2_data), .in2(rom_3_data), .out(multiplexer_1_out), .sel(SEL));  // open: in3
  mod25_sub mod25_sub_1 (.A(multiplexer_1_out), .B(POS), .D(out_4));  // open: out_4

  // Notes on the sheet:
  //   contents of rom_1 (hex, n*v repeats v):
  //   14 16 18 6 0 3 5 f 15 19 1 4 2 a c 13 7 17 12 b 11 8 d 10 e 9
  //   contents of rom_2 (hex, n*v repeats v):
  //   0 9 f 2 19 16 11 b 5 1 3 a e 13 18 14 10 6 4 d 7 7 c 8 15 12
  //   contents of rom_3 (hex, n*v repeats v):
  //   13 0 6 1 f 2 12 3 10 4 14 5 15 d 19 7 18 8 17 9 16 b 11 a e c
  //   bw
endmodule

module rotor_fw (
  input  [5:0] CHAR_IN,
  input  [5:0] POS,
  input  [1:0] SEL,
  output [5:0] out_4
);

  wire [5:0] mod26_add_1_s, multiplexer_1_out, rom_1_data, rom_2_data, rom_3_data;

  mod26_add mod26_add_1 (.A(CHAR_IN), .B(POS), .S(mod26_add_1_s));  // open: out_3, out_5
  ROM #(.addrWidth(6), .dataWidth(6)) rom_1 (.addr(mod26_add_1_s), .data(rom_1_data));
  ROM #(.addrWidth(6), .dataWidth(6)) rom_2 (.addr(mod26_add_1_s), .data(rom_2_data));
  ROM #(.addrWidth(6), .dataWidth(6)) rom_3 (.addr(mod26_add_1_s), .data(rom_3_data));
  Multiplexer #(.select(2), .width(6)) multiplexer_1 (
    .in0(rom_1_data), .in1(rom_2_data), .in2(rom_3_data), .out(multiplexer_1_out), .sel(SEL));  // open: in3
  mod25_sub mod25_sub_1 (.A(multiplexer_1_out), .B(POS), .D(out_4));  // open: out_4

  // Notes on the sheet:
  //   contents of rom_1 (hex, n*v repeats v):
  //   4 a c 5 b 6 3 10 15 19 d 13 e 16 18 7 17 14 12 f 0 8 1 11 2 9
  //   contents of rom_2 (hex, n*v repeats v):
  //   0 9 3 a 12 8 11 14 17 1 b 7 16 13 c 2 10 6 19 d f 18 5 15 e 4
  //   contents of rom_3 (hex, n*v repeats v):
  //   1 3 5 7 9 b 2 f 11 13 17 15 19 d 18 4 8 16 6 0 a c 14 12 10 e
  //   fw
endmodule

module reflector (
  input  [5:0] CHAR_IN,
  output [5:0] CHAR_OUT
);

  ROM #(.addrWidth(6), .dataWidth(6)) rom_1 (.addr(CHAR_IN), .data(CHAR_OUT));

  // Notes on the sheet:
  //   Reflector
  //   contents of rom_1 (hex, n*v repeats v):
  //   18 11 14 7 10 12 b 3 f 17 d 6 e a c 8 4 1 5 19 2 16 15 9 0 13
endmodule

module plugboard (
  input  [5:0] CHAR_IN,
  output [5:0] CHAR_OUT
);

  ROM #(.addrWidth(6), .dataWidth(6)) rom_1 (.addr(CHAR_IN), .data(CHAR_OUT));

  // Notes on the sheet:
  //   contents of rom_1 (hex, n*v repeats v):
  //   15 12 6 b 4 14 2 19 d 9 c 3 a 8 16 f 10 17 1 13 5 0 e 11 18 7
  //   PlugBoard
endmodule

module mod25_sub (
  input  [5:0] A,
  input  [5:0] B,
  output [5:0] D,
  output [5:0] out_4
);

  wire comparator_1_lt;
  wire [5:0] adder_1_out, bit_extender_1_out, bit_extender_2_out, bit_extender_3_out, bit_extender_4_out,
       multiplexer_1_out;

  Bit_Extender #(.in_width(6), .out_width(6), .\type ("zero")) bit_extender_1 (.in(A), .out(bit_extender_1_out));
  Bit_Extender #(.in_width(6), .out_width(6), .\type ("zero")) bit_extender_2 (.in(B), .out(bit_extender_2_out));
  Comparator #(.mode("unsigned"), .width(6)) comparator_1 (
    .a(bit_extender_1_out), .b(bit_extender_2_out), .lt(comparator_1_lt));  // open: gt, eq
  Bit_Extender #(.in_width(6), .out_width(6), .\type ("zero")) bit_extender_3 (
    .in(bit_extender_1_out), .out(bit_extender_3_out));
  Bit_Extender #(.in_width(6), .out_width(6), .\type ("zero")) bit_extender_4 (
    .in(bit_extender_2_out), .out(bit_extender_4_out));
  Adder #(.width(6)) adder_1 (.a(bit_extender_3_out), .b(6'b011010), .out(adder_1_out));  // open: cin, cout
  Multiplexer #(.width(6)) multiplexer_1 (
    .in0(bit_extender_3_out), .in1(adder_1_out), .out(multiplexer_1_out), .sel(comparator_1_lt));
  Subtractor #(.width(6)) subtractor_1 (.a(multiplexer_1_out), .b(bit_extender_4_out), .out(D));  // open: bin, bout

  assign out_4 = B;
endmodule

module mod26_add (
  input  [5:0] A,
  input  [5:0] B,
  output [5:0] out_3,
  output [5:0] S,
  output [5:0] out_5
);

  wire comparator_1_eq, comparator_1_gt, or_1_out;
  wire [5:0] adder_1_out, subtractor_1_out;

  Bit_Extender #(.in_width(6), .out_width(6), .\type ("zero")) bit_extender_1 (.in(A), .out(out_3));
  Bit_Extender #(.in_width(6), .out_width(6), .\type ("zero")) bit_extender_2 (.in(B), .out(out_5));
  Adder #(.width(6)) adder_1 (.a(out_3), .b(out_5), .out(adder_1_out));  // open: cin, cout
  Comparator #(.mode("unsigned"), .width(6)) comparator_1 (
    .a(adder_1_out), .b(6'b011010), .gt(comparator_1_gt), .eq(comparator_1_eq));  // open: lt
  or or_1 (or_1_out, comparator_1_gt, comparator_1_eq);
  Subtractor #(.width(6)) subtractor_1 (.a(adder_1_out), .b(6'b011010), .out(subtractor_1_out));  // open: bin, bout
  Multiplexer #(.width(6)) multiplexer_1 (.in0(adder_1_out), .in1(subtractor_1_out), .out(S), .sel(or_1_out));
endmodule
