// Logisim project mod26_add.circ as structural Verilog: 1 circuit, main circuit main
module main (
  input  [5:0] in_1,
  input  [5:0] in_2,
  output [5:0] out_3
);

  wire comparator_1_eq, comparator_1_gt, or_1_out;
  wire [5:0] adder_1_out, bit_extender_1_out, bit_extender_2_out, negator_1_out, subtractor_1_out;

  Bit_Extender #(.in_width(6), .out_width(6), .\type ("zero")) bit_extender_1 (.in(in_1), .out(bit_extender_1_out));
  Bit_Extender #(.in_width(6), .out_width(6), .\type ("zero")) bit_extender_2 (.in(in_2), .out(bit_extender_2_out));
  Adder #(.width(6)) adder_1 (.a(bit_extender_1_out), .b(bit_extender_2_out), .out(adder_1_out));  // open: cin, cout
  Comparator #(.mode("unsigned"), .width(6)) comparator_1 (
    .a(adder_1_out), .b(6'b011010), .gt(comparator_1_gt), .eq(comparator_1_eq));  // open: lt
  or or_1 (or_1_out, comparator_1_gt, comparator_1_eq);
  Subtractor #(.width(6)) subtractor_1 (.a(adder_1_out), .b(6'b011010), .out(subtractor_1_out));  // open: bin, bout
  Negator #(.width(6)) negator_1 (.in(subtractor_1_out), .out(negator_1_out));
  Multiplexer #(.width(6)) multiplexer_1 (.in0(adder_1_out), .in1(negator_1_out), .out(out_3), .sel(or_1_out));
endmodule
