// Logisim project mod26_sub.circ as structural Verilog: 1 circuit, main circuit main
module main (
  input  [5:0] a1,
  input  [5:0] b1,
  output [5:0] output1
);

  wire comparator_1_lt;
  wire [5:0] adder_1_out, bit_extender_1_out, bit_extender_2_out, multiplexer_1_out;

  Comparator #(.mode("unsigned"), .width(5)) comparator_1 (
    .a(a1[4:0]), .b(b1[4:0]), .lt(comparator_1_lt));  // open: gt, eq
  Bit_Extender #(.in_width(6), .out_width(6), .\type ("zero")) bit_extender_1 (.in(a1), .out(bit_extender_1_out));
  Bit_Extender #(.in_width(6), .out_width(6), .\type ("zero")) bit_extender_2 (.in(b1), .out(bit_extender_2_out));
  Adder #(.width(6)) adder_1 (.a(bit_extender_1_out), .b(6'b011010), .out(adder_1_out));  // open: cin, cout
  Multiplexer #(.width(6)) multiplexer_1 (
    .in0(bit_extender_1_out), .in1(adder_1_out), .out(multiplexer_1_out), .sel(comparator_1_lt));
  Subtractor #(.width(6)) subtractor_1 (
    .a(multiplexer_1_out), .b(bit_extender_2_out), .out(output1));  // open: bin, bout
  // Probe on output1
  // Pins of 5 and 6 bits meet at a1
  // Pins of 5 and 6 bits meet at b1
endmodule
