// Logisim project Reflector.circ as structural Verilog: 1 circuit, main circuit main
module main (
  input  [5:0] in_1,
  output [5:0] out_2
);

  ROM #(.addrWidth(6), .dataWidth(6)) rom_1 (.addr(in_1), .data(out_2));

  // Notes on the sheet:
  //   contents of rom_1 (hex, n*v repeats v):
  //   18 11 14 7 10 12 b 3 f 17 d 6 e a c 8 4 1 5 19 2 16 15 9 0 13 1a 1b 1c 1d 1e 1f
endmodule
