// Logisim project cipher_path.circ as structural Verilog: 5 circuits, main circuit plugboard
module main (
  input  [4:0] CHAR_IN,
  input  [4:0] pos1,
  input  [4:0] pos2,
  input  [4:0] pos3,
  output [4:0] CHAR_OUT
);

  wire [4:0] plugboard_1_char_out, reflector_1_char_out, rotor_bw_1_char_out, rotor_bw_2_char_out,
       rotor_bw_3_char_out, rotor_fw_1_char_out, rotor_fw_2_char_out, rotor_fw_3_char_out;

  plugboard plugboard_1 (.CHAR_IN(CHAR_IN), .CHAR_OUT(plugboard_1_char_out));
  rotor_fw rotor_fw_1 (.CHAR_IN(plugboard_1_char_out), .POS(pos1), .SEL(2'b10), .CHAR_OUT(rotor_fw_1_char_out));
  rotor_fw rotor_fw_2 (.CHAR_IN(rotor_fw_1_char_out), .POS(pos2), .SEL(2'b01), .CHAR_OUT(rotor_fw_2_char_out));
  rotor_fw rotor_fw_3 (.CHAR_IN(rotor_fw_2_char_out), .POS(pos3), .SEL(2'b00), .CHAR_OUT(rotor_fw_3_char_out));
  reflector reflector_1 (.CHAR_IN(rotor_fw_3_char_out), .CHAR_OUT(reflector_1_char_out));
  rotor_bw rotor_bw_1 (.CHAR_IN(reflector_1_char_out), .POS(pos1), .SEL(2'b00), .CHAR_OUT(rotor_bw_1_char_out));
  rotor_bw rotor_bw_2 (.CHAR_IN(rotor_bw_1_char_out), .POS(pos2), .SEL(2'b01), .CHAR_OUT(rotor_bw_2_char_out));
  rotor_bw rotor_bw_3 (.CHAR_IN(rotor_bw_2_char_out), .POS(pos3), .SEL(2'b10), .CHAR_OUT(rotor_bw_3_char_out));
  plugboard plugboard_2 (.CHAR_IN(rotor_bw_3_char_out), .CHAR_OUT(CHAR_OUT));

  // Notes on the sheet:
  //   Cipher_path
endmodule

module plugboard (
  input  [4:0] CHAR_IN,
  output [4:0] CHAR_OUT
);

  ROM #(.addrWidth(5), .dataWidth(5)) rom_1 (.addr(CHAR_IN), .data(CHAR_OUT));

  // Notes on the sheet:
  //   contents of rom_1 (hex, n*v repeats v):
  //   5 11 17 16 a 0 6 7 8 9 4 b c d e f 10 1 12 13 14 15 3 2 18 19 1a 1b 1c 1d 1e 1f
  //   PlugBoard
endmodule

module reflector (
  input  [4:0] CHAR_IN,
  output [4:0] CHAR_OUT
);

  ROM #(.addrWidth(5), .dataWidth(5)) rom_1 (.addr(CHAR_IN), .data(CHAR_OUT));

  // Notes on the sheet:
  //   Reflector
  //   contents of rom_1 (hex, n*v repeats v):
  //   18 11 14 7 10 12 b 3 f 17 d 6 e a c 8 4 1 5 19 2 16 15 9 0 13 1a 1b 1c 1d 1e 1f
endmodule

module rotor_fw (
  input  [4:0] CHAR_IN,
  input  [4:0] POS,
  input  [1:0] SEL,
  output [4:0] CHAR_OUT
);

  wire comparator_1_eq, comparator_1_gt, comparator_2_lt, or_1_out;
  wire [4:0] multiplexer_2_out, rom_1_data, rom_2_data, rom_3_data;
  wire [5:0] adder_1_out, adder_2_out, bit_extender_1_out, bit_extender_2_out, bit_extender_3_out,
       bit_extender_4_out, multiplexer_1_out, multiplexer_3_out, subtractor_1_out;
  wire [5:5] subtractor_2_out;

  // Probe on CHAR_OUT
  // Probe on CHAR_IN
  // Probe on POS
  assign bit_extender_1_out = {{1{1'b0}}, CHAR_IN};  // Bit_Extender bit_extender_1
  assign bit_extender_2_out = {{1{1'b0}}, POS};  // Bit_Extender bit_extender_2
  Adder #(.width(6)) adder_1 (.a(bit_extender_1_out), .b(bit_extender_2_out), .out(adder_1_out));  // open: cin, cout
  Comparator #(.mode("unsigned"), .width(6)) comparator_1 (
    .a(adder_1_out), .b(6'b011010), .gt(comparator_1_gt), .eq(comparator_1_eq));  // open: lt
  or or_1 (or_1_out, comparator_1_gt, comparator_1_eq);
  Subtractor #(.width(6)) subtractor_1 (.a(adder_1_out), .b(6'b011010), .out(subtractor_1_out));  // open: bin, bout
  Multiplexer #(.width(6)) multiplexer_1 (
    .in0(adder_1_out), .in1(subtractor_1_out), .out(multiplexer_1_out), .sel(or_1_out));
  ROM #(.addrWidth(5), .dataWidth(5)) rom_1 (.addr(multiplexer_1_out[4:0]), .data(rom_1_data));
  ROM #(.addrWidth(5), .dataWidth(5)) rom_2 (.addr(multiplexer_1_out[4:0]), .data(rom_2_data));
  ROM #(.addrWidth(5), .dataWidth(5)) rom_3 (.addr(multiplexer_1_out[4:0]), .data(rom_3_data));
  Multiplexer #(.select(2), .width(5)) multiplexer_2 (
    .in0(rom_1_data), .in1(rom_2_data), .in2(rom_3_data), .out(multiplexer_2_out), .sel(SEL));  // open: in3
  Comparator #(.mode("unsigned"), .width(5)) comparator_2 (
    .a(multiplexer_2_out), .b(POS), .lt(comparator_2_lt));  // open: gt, eq
  assign bit_extender_3_out = {{1{1'b0}}, multiplexer_2_out};  // Bit_Extender bit_extender_3
  assign bit_extender_4_out = {{1{1'b0}}, POS};  // Bit_Extender bit_extender_4
  Adder #(.width(6)) adder_2 (.a(bit_extender_3_out), .b(6'b011010), .out(adder_2_out));  // open: cin, cout
  Multiplexer #(.width(6)) multiplexer_3 (
    .in0(bit_extender_3_out), .in1(adder_2_out), .out(multiplexer_3_out), .sel(comparator_2_lt));
  Subtractor #(.width(6)) subtractor_2 (
    .a(multiplexer_3_out), .b(bit_extender_4_out), .out({subtractor_2_out[5], CHAR_OUT}));  // open: bin, bout

  // Notes on the sheet:
  //   rotor_fw
  //   contents of rom_1 (hex, n*v repeats v):
  //   4 a c 5 b 6 3 10 15 19 d 13 e 16 18 7 17 14 12 f 0 8 1 11 2 9 1a 1b 1c 1d 1e 1f
  //   contents of rom_2 (hex, n*v repeats v):
  //   0 9 3 a 12 8 11 14 17 1 b 7 16 13 c 2 10 6 19 d f 18 5 15 e 4 1a 1b 1c 1d 1e 1f
  //   contents of rom_3 (hex, n*v repeats v):
  //   1 3 5 7 9 b 2 f 11 13 17 15 19 d 18 4 8 16 6 0 a c 14 12 10 e 1a 1b 1c 1d 1e 1f
endmodule

module rotor_bw (
  input  [4:0] CHAR_IN,
  input  [4:0] POS,
  input  [1:0] SEL,
  output [4:0] CHAR_OUT
);

  wire comparator_1_eq, comparator_1_gt, comparator_2_lt, or_1_out;
  wire [4:0] multiplexer_2_out, rom_1_data, rom_2_data, rom_3_data;
  wire [5:0] adder_1_out, adder_2_out, bit_extender_1_out, bit_extender_2_out, bit_extender_3_out,
       bit_extender_4_out, multiplexer_1_out, multiplexer_3_out, subtractor_1_out;
  wire [5:5] subtractor_2_out;

  // Probe on CHAR_IN
  // Probe on POS
  // Probe on CHAR_OUT
  assign bit_extender_1_out = {{1{1'b0}}, CHAR_IN};  // Bit_Extender bit_extender_1
  assign bit_extender_2_out = {{1{1'b0}}, POS};  // Bit_Extender bit_extender_2
  Adder #(.width(6)) adder_1 (.a(bit_extender_1_out), .b(bit_extender_2_out), .out(adder_1_out));  // open: cin, cout
  Comparator #(.mode("unsigned"), .width(6)) comparator_1 (
    .a(adder_1_out), .b(6'b011010), .gt(comparator_1_gt), .eq(comparator_1_eq));  // open: lt
  Subtractor #(.width(6)) subtractor_1 (.a(adder_1_out), .b(6'b011010), .out(subtractor_1_out));  // open: bin, bout
  or or_1 (or_1_out, comparator_1_gt, comparator_1_eq);
  Multiplexer #(.width(6)) multiplexer_1 (
    .in0(adder_1_out), .in1(subtractor_1_out), .out(multiplexer_1_out), .sel(or_1_out));
  ROM #(.addrWidth(5), .dataWidth(5)) rom_1 (.addr(multiplexer_1_out[4:0]), .data(rom_1_data));
  ROM #(.addrWidth(5), .dataWidth(5)) rom_2 (.addr(multiplexer_1_out[4:0]), .data(rom_2_data));
  ROM #(.addrWidth(5), .dataWidth(5)) rom_3 (.addr(multiplexer_1_out[4:0]), .data(rom_3_data));
  Multiplexer #(.select(2), .width(5)) multiplexer_2 (
    .in0(rom_1_data), .in1(rom_2_data), .in2(rom_3_data), .out(multiplexer_2_out), .sel(SEL));  // open: in3
  Comparator #(.mode("unsigned"), .width(5)) comparator_2 (
    .a(multiplexer_2_out), .b(POS), .lt(comparator_2_lt));  // open: gt, eq
  assign bit_extender_3_out = {{1{1'b0}}, multiplexer_2_out};  // Bit_Extender bit_extender_3
  assign bit_extender_4_out = {{1{1'b0}}, POS};  // Bit_Extender bit_extender_4
  Adder #(.width(6)) adder_2 (.a(bit_extender_3_out), .b(6'b011010), .out(adder_2_out));  // open: cin, cout
  Multiplexer #(.width(6)) multiplexer_3 (
    .in0(bit_extender_3_out), .in1(adder_2_out), .out(multiplexer_3_out), .sel(comparator_2_lt));
  Subtractor #(.width(6)) subtractor_2 (
    .a(multiplexer_3_out), .b(bit_extender_4_out), .out({subtractor_2_out[5], CHAR_OUT}));  // open: bin, bout

  // Notes on the sheet:
  //   contents of rom_1 (hex, n*v repeats v):
  //   14 16 18 6 0 3 5 f 15 19 1 4 2 a c 13 7 17 12 b 11 8 d 10 e 9 1a 1b 1c 1d 1e 1f
  //   contents of rom_2 (hex, n*v repeats v):
  //   0 9 f 2 19 16 11 b 5 1 3 a e 13 18 14 10 6 4 d 7 17 6 8 15 12 1a 1b 1c 1d 1e 1f
  //   contents of rom_3 (hex, n*v repeats v):
  //   13 0 6 1 f 2 12 3 10 4 14 5 15 d 19 7 18 8 17 9 16 b 11 a e c 1a 1b 1c 1d 1e 1f
endmodule
