// Logisim project complete_fw.circ as structural Verilog: 1 circuit, main circuit main
module main (
  input  [5:0] CHAR_IN,
  input  [5:0] POS,
  input  [1:0] SEL,
  output [5:0] output1
);

  wire comparator_1_eq, comparator_1_gt, comparator_2_lt, or_1_out;
  wire [4:0] multiplexer_2_out, rom_1_data, rom_2_data, rom_3_data;
  wire [5:0] adder_1_out, adder_2_out, bit_extender_1_out, bit_extender_2_out, bit_extender_3_out,
       bit_extender_4_out, multiplexer_1_out, multiplexer_3_out, subtractor_1_out;

  // Probe on output1
  // Probe on CHAR_IN
  // Probe on POS
  Bit_Extender #(.in_width(6), .out_width(6), .\type ("zero")) bit_extender_1 (.in(CHAR_IN), .out(bit_extender_1_out));
  Bit_Extender #(.in_width(6), .out_width(6), .\type ("zero")) bit_extender_2 (.in(POS), .out(bit_extender_2_out));
  Adder #(.width(6)) adder_1 (.a(bit_extender_1_out), .b(bit_extender_2_out), .out(adder_1_out));  // open: cin, cout
  Comparator #(.mode("unsigned"), .width(6)) comparator_1 (
    .a(adder_1_out), .b(6'b011010), .gt(comparator_1_gt), .eq(comparator_1_eq));  // open: lt
  or or_1 (or_1_out, comparator_1_gt, comparator_1_eq);
  Subtractor #(.width(6)) subtractor_1 (.a(adder_1_out), .b(6'b011010), .out(subtractor_1_out));  // open: bin, bout
  Multiplexer #(.width(6)) multiplexer_1 (
    .in0(adder_1_out), .in1(subtractor_1_out), .out(multiplexer_1_out), .sel(or_1_out));
  ROM #(.addrWidth(5), .dataWidth(5)) rom_1 (.addr(multiplexer_1_out[4:0]), .data(rom_1_data));
  ROM #(.addrWidth(5), .dataWidth(5)) rom_2 (.addr(multiplexer_1_out[4:0]), .data(rom_2_data));
  ROM #(.addrWidth(5), .dataWidth(5)) rom_3 (.addr(multiplexer_1_out[4:0]), .data(rom_3_data));
  Multiplexer #(.select(2), .width(5)) multiplexer_2 (
    .in0(rom_1_data), .in1(rom_2_data), .in2(rom_3_data), .out(multiplexer_2_out), .sel(SEL));  // open: in3
  Comparator #(.mode("unsigned"), .width(5)) comparator_2 (
    .a(multiplexer_2_out), .b(POS[4:0]), .lt(comparator_2_lt));  // open: gt, eq
  assign bit_extender_3_out = {{1{1'b0}}, multiplexer_2_out};  // Bit_Extender bit_extender_3
  Bit_Extender #(.in_width(6), .out_width(6), .\type ("zero")) bit_extender_4 (.in(POS), .out(bit_extender_4_out));
  Adder #(.width(6)) adder_2 (.a(bit_extender_3_out), .b(6'b011010), .out(adder_2_out));  // open: cin, cout
  Multiplexer #(.width(6)) multiplexer_3 (
    .in0(bit_extender_3_out), .in1(adder_2_out), .out(multiplexer_3_out), .sel(comparator_2_lt));
  Subtractor #(.width(6)) subtractor_2 (
    .a(multiplexer_3_out), .b(bit_extender_4_out), .out(output1));  // open: bin, bout
  // Pins of 5 and 6 bits meet at POS

  // Notes on the sheet:
  //   contents of rom_1 (hex, n*v repeats v):
  //   4 a c 5 b 6 3 10 15 19 d 13 e 16 18 7 17 14 12 f 0 8 1 11 2 9 1a 1b 1c 1d 1e 1f
  //   contents of rom_2 (hex, n*v repeats v):
  //   0 9 3 a 12 8 11 14 17 1 b 7 16 13 c 2 10 6 19 d f 18 5 15 e 4 1a 1b 1c 1d 1e 1f
  //   contents of rom_3 (hex, n*v repeats v):
  //   1 3 5 7 9 b 2 f 11 13 17 15 19 d 18 4 8 16 6 0 a c 14 12 10 e 1a 1b 1c 1d 1e 1f
endmodule
