// Logisim project display_decoder.circ as structural Verilog: 1 circuit, main circuit main
module main (
  input  [4:0] CHAR_IN
);

  wire sA, sB, sC, sD, sE, sF, sG;

  ROM #(.addrWidth(5), .dataWidth(7)) rom_1 (.addr(CHAR_IN), .data({sA, sB, sC, sD, sE, sF, sG}));
  _7_Segment_Display u_7_segment_display_1 (.g(sG), .f(sF), .a(sA), .b(sB), .e(sE), .d(sD), .c(sC));  // open: dp

  // Notes on the sheet:
  //   contents of rom_1 (hex, n*v repeats v):
  //   77 1f 4e 3d 4f 47 5e 37 30 38 57 e 76 15 1e 67 73 5 5b f 3e 1c 7a 37 3b 6d
endmodule
