// Logisim project enigma_all.circ as structural Verilog: 10 circuits, main circuit enigma_top
module mod26_add (
  input  [4:0] A,
  input  [4:0] B,
  output [4:0] S
);

  wire adder_1_p3, bit_extender_1_p1, bit_extender_2_p2, comparator_1_p3, multiplexer_1_p4, subtractor_1_p3;

  // Bit_Extender #(.in_width(5), .out_width(6), .\type ("zero")) bit_extender_1: pin names not known; wires that end beside it: bit_extender_1_p1
  // Bit_Extender #(.in_width(5), .out_width(6), .\type ("zero")) bit_extender_2: pin names not known; wires that end beside it: B, bit_extender_2_p2
  // Adder #(.width(6)) adder_1: pin names not known; wires that end beside it: bit_extender_1_p1, bit_extender_2_p2, adder_1_p3
  // Subtractor #(.width(6)) subtractor_1: pin names not known; wires that end beside it: adder_1_p3, 6'b011010, subtractor_1_p3
  // Comparator #(.width(6), .mode("unsigned")) comparator_1: pin names not known; wires that end beside it: adder_1_p3, 6'b011010, comparator_1_p3
  // Multiplexer #(.width(6), .select(1)) multiplexer_1: pin names not known; wires that end beside it: subtractor_1_p3, comparator_1_p3, adder_1_p3, multiplexer_1_p4
  // Bit_Selector #(.in_width(6), .out_width(5), .low_bit(0)) bit_selector_1: pin names not known; wires that end beside it: adder_1_p3, multiplexer_1_p4, S
endmodule

module mod26_sub (
  input  [4:0] A,
  input  [4:0] B,
  output [4:0] D
);

  wire comparator_1_p3, multiplexer_1_p4, subtractor_2_p1, subtractor_2_p3;
  wire [4:0] subtractor_1_p3;
  wire [5:0] undriven, undriven_2;

  // Subtractor #(.width(5)) subtractor_1: pin names not known; wires that end beside it: 5'b11010, B, subtractor_1_p3
  Bit_Extender #(.in_width(5), .out_width(6), .\type ("zero")) bit_extender_1 (.in(A));  // open: out
  Bit_Extender #(.in_width(5), .out_width(6), .\type ("zero")) bit_extender_2 (.in(subtractor_1_p3));  // open: out
  Adder #(.width(6)) adder_1 (.a(undriven), .b(undriven_2));  // open: out, cin, cout
  // Subtractor #(.width(6)) subtractor_2: pin names not known; wires that end beside it: subtractor_2_p1, 6'b011010, subtractor_2_p3
  // Comparator #(.width(6), .mode("unsigned")) comparator_1: pin names not known; wires that end beside it: subtractor_2_p1, 6'b011010, comparator_1_p3
  // Multiplexer #(.width(6), .select(1)) multiplexer_1: pin names not known; wires that end beside it: subtractor_2_p3, subtractor_2_p1, comparator_1_p3, multiplexer_1_p4
  // Bit_Selector #(.in_width(6), .out_width(5), .low_bit(0)) bit_selector_1: pin names not known; wires that end beside it: subtractor_2_p3, subtractor_2_p1, multiplexer_1_p4, D
endmodule

module plugboard (
  input  [4:0] char_in,
  output [4:0] char_out
);

  ROM #(.addrWidth(5), .dataWidth(5)) rom_1 ();  // open: addr, data

  // Notes on the sheet:
  //   contents of rom_1 (hex, n*v repeats v):
  //   0 05 11 17 16 0a 00 06 07 08 09 04 0b 0c 0d 0e 0f 10 10 01 12 13 14 15 03 02 18 19
endmodule

module reflector (
  input  [4:0] char_in,
  output [4:0] char_out
);

  ROM #(.addrWidth(5), .dataWidth(5)) rom_1 ();  // open: addr, data

  // Notes on the sheet:
  //   contents of rom_1 (hex, n*v repeats v):
  //   0 18 11 14 07 10 12 0b 03 0f 17 0d 06 0e 0a 0c 08 10 04 01 05 19 02 16 15 09 00 13
endmodule

module rotor_fw (
  input  [4:0] char_in,
  input  [4:0] pos,
  input  [1:0] sel,
  output [4:0] char_out
);

  // rotor_fw_part rotor_fw_1: pin names not known; wires that end beside it: char_in, pos, sel
  ROM #(.addrWidth(5), .dataWidth(5)) ROM_I_fw ();  // open: addr, data
  ROM #(.addrWidth(5), .dataWidth(5)) ROM_II_fw ();  // open: addr, data
  ROM #(.addrWidth(5), .dataWidth(5)) ROM_III_fw ();  // open: addr, data
  Multiplexer #(.width(5), .select(2)) multiplexer_1 ();  // open: in0, in1, in2, in3, out, sel

  // Notes on the sheet:
  //   contents of ROM_I_fw (hex, n*v repeats v):
  //   0 04 0a 0c 05 0b 06 03 10 15 19 0d 13 0e 16 18 07 10 17 14 12 0f 00 08 01 11 02 09
  //   contents of ROM_II_fw (hex, n*v repeats v):
  //   0 00 09 03 0a 12 08 11 14 17 01 0b 07 16 13 0c 02 10 10 06 19 0d 0f 18 05 15 0e 04
  //   contents of ROM_III_fw (hex, n*v repeats v):
  //   0 01 03 05 07 09 0b 02 0f 11 13 17 15 19 0d 18 04 10 08 16 06 00 0a 0c 14 12 10 0e
endmodule

module rotor_bw (
  input  [4:0] char_in,
  input  [4:0] pos,
  input  [1:0] sel,
  output [4:0] char_out
);

  ROM #(.addrWidth(5), .dataWidth(5)) ROM_I_bw ();  // open: addr, data
  ROM #(.addrWidth(5), .dataWidth(5)) ROM_II_bw ();  // open: addr, data
  ROM #(.addrWidth(5), .dataWidth(5)) ROM_III_bw ();  // open: addr, data
  Multiplexer #(.width(5), .select(2)) multiplexer_1 ();  // open: in0, in1, in2, in3, out, sel

  // Notes on the sheet:
  //   contents of ROM_I_bw (hex, n*v repeats v):
  //   0 14 16 18 06 00 03 05 0f 15 19 01 04 02 0a 0c 13 10 07 17 12 0b 11 08 0d 10 0e 09
  //   contents of ROM_II_bw (hex, n*v repeats v):
  //   0 00 09 0f 02 19 16 11 0b 05 01 03 0a 0e 13 18 14 10 10 06 04 0d 07 17 0c 08 15 12
  //   contents of ROM_III_bw (hex, n*v repeats v):
  //   0 13 00 06 01 0f 02 12 03 10 04 14 05 15 0d 19 07 10 18 08 17 09 16 0b 11 0a 0e 0c
endmodule

module stepping (
  input  CLK,
  input  RST,
  input  KEYPRESS,
  output [4:0] POS1,
  output [4:0] POS2,
  output [4:0] POS3
);

  wire comparator_1_eq, comparator_2_p3, or_1_out, Rotor_I_p2, Rotor_II_p2, Rotor_II_p3, Rotor_III_p2;

  // NOT_Gate not_1 has open pins: in=RST, out=open
  // Counter #(.width(5), .max(25)) Rotor_III: pin names not known; wires that end beside it: KEYPRESS, Rotor_III_p2, CLK, 5'b10101
  // Counter #(.width(5), .max(25)) Rotor_II: pin names not known; wires that end beside it: CLK, Rotor_II_p2, Rotor_II_p3
  // Counter #(.width(5), .max(25)) Rotor_I: pin names not known; wires that end beside it: CLK, Rotor_I_p2, Rotor_III_p2
  Comparator #(.width(5), .mode("unsigned")) comparator_1 (.a(POS1), .eq(comparator_1_eq));  // open: b, gt, lt
  // Comparator #(.width(5), .mode("unsigned")) comparator_2: pin names not known; wires that end beside it: POS2, 5'b01100, comparator_2_p3
  or or_1 (or_1_out, comparator_1_eq, comparator_2_p3);
  // AND_Gate and_1: pin names not known; wires that end beside it: KEYPRESS, or_1_out, Rotor_II_p2
  // AND_Gate and_2: pin names not known; wires that end beside it: comparator_2_p3, KEYPRESS, Rotor_I_p2
endmodule

module cipher_path (
  input  [4:0] char_in,
  input  [4:0] pos1,
  input  [4:0] pos2,
  input  [4:0] pos3,
  output [4:0] char_out
);

  // plugboard_part plugboard_1: pin names not known; wires that end beside it: char_in, pos1, pos2, pos3
  // rotor_fw_part rotor_fw_1: pin names not known; wires that end beside it: 2'b11
  // rotor_fw_part rotor_fw_2: pin names not known; wires that end beside it: 2'b10
  // rotor_fw_part rotor_fw_3: pin names not known; wires that end beside it: 2'b01
  // reflector_part reflector_1: pin names not known
  // rotor_bw_part rotor_bw_1: pin names not known; wires that end beside it: 2'b01
  // rotor_bw_part rotor_bw_2: pin names not known; wires that end beside it: 2'b10
  // rotor_bw_part rotor_bw_3: pin names not known; wires that end beside it: 2'b11
  // plugboard_part plugboard_2: pin names not known; wires that end beside it: char_out
endmodule

module enigma_top (
  input  CLK,
  input  RST,
  input  KEYPRESS,
  input  [4:0] char_in,
  output [4:0] char_out,
  output valid_out
);

  wire display_decoder_1_p3, display_decoder_1_p5, display_decoder_1_p6, display_decoder_1_p7,
       display_decoder_1_p8, display_decoder_1_p9, display_decoder_1_p10, display_decoder_1_p11,
       stepping_1_p5, stepping_1_p6, stepping_1_p7;

  // stepping_part stepping_1: pin names not known; wires that end beside it: CLK, RST, KEYPRESS, char_in, stepping_1_p5, stepping_1_p6, stepping_1_p7
  // cipher_path_part cipher_path_1: pin names not known
  Register #(.width(5)) out_reg ();  // open: D, en, Q, clk, clr
  Register #(.width(1)) valid_reg ();  // open: D, en, Q, clk, clr
  // display_decoder_part display_decoder_1: pin names not known; wires that end beside it: valid_out, char_out, display_decoder_1_p3, display_decoder_1_p3, display_decoder_1_p5, display_decoder_1_p6, display_decoder_1_p7, display_decoder_1_p8, display_decoder_1_p9, display_decoder_1_p10, display_decoder_1_p11, display_decoder_1_p5
  // Hex_Digit_Display POS1_III: pin names not known; wires that end beside it: stepping_1_p5
  // Hex_Digit_Display POS2_II: pin names not known; wires that end beside it: stepping_1_p6
  Hex_Digit_Display POS3_I ();  // open: value, dp
  // _7_Segment_Display #(.active("true")) 7_segment_display_1: pin names not known; wires that end beside it: display_decoder_1_p6, display_decoder_1_p7, display_decoder_1_p8, display_decoder_1_p9, display_decoder_1_p10, display_decoder_1_p11
endmodule

module display_decoder (
  input  [4:0] char,
  output [6:0] seg
);

  ROM #(.addrWidth(5), .dataWidth(7)) rom_1 ();  // open: addr, data

  // Notes on the sheet:
  //   contents of rom_1 (hex, n*v repeats v):
  //   0 77 1f 4e 3d 4f 47 5f 37 06 3c 37 0e 76 15 3f 67 10 73 05 5b 0f 3e 1c 14 37 33 6d
endmodule
