// Logisim project stepping.circ as structural Verilog: 1 circuit, main circuit main
module main (
  input  CLK,
  input  RST,
  input  KEYPRESS,
  output [4:0] POS11,
  output [4:0] POS22,
  output [4:0] POS33
);

  wire and_1_out, and_2_out, comparator_1_eq, comparator_2_eq, or_1_out;

  Counter #(.max('h19), .width(5)) POS1 (
    .clr(RST), .up(KEYPRESS), .clk(CLK), .Q(POS11));  // open: load, count, D, carry
  Counter #(.max('h19), .width(5)) POS2 (
    .clr(RST), .count(and_1_out), .clk(CLK), .Q(POS22));  // open: load, up, D, carry
  Counter #(.max('h19), .width(5)) POS3 (
    .clr(RST), .count(and_2_out), .clk(CLK), .Q(POS33));  // open: load, up, D, carry
  Comparator #(.mode("unsigned"), .width(5)) comparator_1 (
    .a(POS11), .b(5'b10101), .eq(comparator_1_eq));  // open: gt, lt
  Comparator #(.mode("unsigned"), .width(5)) comparator_2 (
    .a(POS22), .b(5'b01100), .eq(comparator_2_eq));  // open: gt, lt
  or or_1 (or_1_out, comparator_1_eq, comparator_2_eq);
  and and_1 (and_1_out, or_1_out, KEYPRESS);
  and and_2 (and_2_out, comparator_2_eq, KEYPRESS);
endmodule
